# Fritzing sketch Wiring Diagram (saved by Fritzing 0.9.3b)
breadboards: 2

parts:
  Componente1 = Arduino Nano (Rev3.0)
  Componente2 = Motor Driver 1A Dual TB6612FNG
  LED1 = LED - 5mm [color="Green (555nm)" package="5 mm [THT]"]
  HC-SR04_Sensor_1 = HC-SR04 Ultrasonic Distance Sensor
  HC-SR04_Sensor_2 = HC-SR04 Ultrasonic Distance Sensor
  HC-SR04_Sensor_3 = HC-SR04 Ultrasonic Distance Sensor
  HC-SR04_Sensor_4 = HC-SR04 Ultrasonic Distance Sensor
  M2 = DC Motor
  S1 = Pushbutton [package="[THT]"]
  R1 = Resistor [tolerance=±5% resistance=330 package="2010 [SMD]"]
  R2 = Resistor [tolerance=±5% resistance=330 package="2010 [SMD]"]
  J1 = Basic Servo
  C1 = Capacitor [package=cap-pth-small2]
  C2 = Capacitor [package=cap-pth-small2]
  Q1 = Basic FET P-Channel [package="TO220 [THT]"]
  C3 = Electrolytic Capacitor [capacitance=1µF package="100 mil [THT, electrolytic]"]

nets:
  GND: Componente1.GND, Componente2.STBY, HC-SR04_Sensor_1.GND, HC-SR04_Sensor_2.GND, HC-SR04_Sensor_3.GND, HC-SR04_Sensor_4.GND
  N1: Componente1.D2, Componente2.AIN1
  N2: Componente1.D3, Componente2.PWMA
  N3: Componente1.D4, Componente2.AIN2
  N4: Componente1.D5, S1.Pin_1, S1.Pin_2, R1.Pin_1
  N5: Componente1.D6, J1.pulse
  N6: Componente1.D7, HC-SR04_Sensor_1.ECHO
  N7: Componente1.D8, HC-SR04_Sensor_1.TRIG
  N8: Componente1.D9, HC-SR04_Sensor_3.ECHO
  N9: Componente1.D10, HC-SR04_Sensor_3.TRIG
  N10: Componente1.D11/MOSI, HC-SR04_Sensor_2.TRIG
  N11: Componente1.D12/MISO, HC-SR04_Sensor_2.ECHO
  VCC: Componente1.VIN, Componente2.VCC, HC-SR04_Sensor_4.VCC
  N12: Componente1.A0, HC-SR04_Sensor_4.TRIG
  N13: Componente1.D13/SCK, HC-SR04_Sensor_4.ECHO
  GND_2: Componente2.GND, Componente2.VM, R2.Pin_0, J1.gnd, C1.1, C1.2, C2.2, Q1.source, C3.-
  N14: Componente2.A02, M2.pin_1
  N15: Componente2.A01, M2.pin_2
  N16: LED1.cathode, S1.Pin_3, S1.Pin_4, J1.vcc, C2.1, Q1.gate, C3.+
  N17: LED1.anode, R2.Pin_1
  VCC_2: HC-SR04_Sensor_1.VCC, HC-SR04_Sensor_2.VCC, HC-SR04_Sensor_3.VCC
